# Fritzing sketch v3 - Phase Switches (saved by Fritzing 0.9.2b)
breadboards: 1

parts:
  L1 = Inductor [inductance=0.38mH package="400 mil [THT]"]
  L2 = Inductor [inductance=0.78mH package="400 mil [THT]"]
  L3 = Inductor [inductance=0.25mH package="400 mil [THT]"]
  Tweeter = Loudspeaker [part_number=8Ω]
  Woofer_1 = Loudspeaker [part_number=4Ω]
  R2 = Resistor [tolerance=±5% resistance=20 package=THT]
  R4 = Resistor [tolerance=±5% resistance=20 package=THT]
  C3 = Electrolytic Capacitor [capacitance=10.61µF voltage=0.1kV package="300 mil [THT, electrolytic]"]
  C1 = Electrolytic Capacitor [capacitance=5.31µF voltage=0.1kV package="300 mil [THT, electrolytic]"]
  Input = Screw terminal - 2 pins [package=THT]
  R1 = Resistor [tolerance=±5% resistance=2 package=THT]
  R3 = Resistor [tolerance=±5% resistance=2 package=THT]
  Attenuation = DPDT Toggle Switch
  Attenuation_2 = DPDT Toggle Switch
  C2 = Electrolytic Capacitor [capacitance=15.92µF voltage=0.1kV package="300 mil [THT, electrolytic]"]
  Tweeter_2 = Screw terminal - 2 pins [package=THT]
  Woofer_1_2 = Screw terminal - 2 pins [package=THT]
  Phase = DPDT Toggle Switch
  Woofer_2 = Loudspeaker [part_number=4Ω]
  Woofer_2_2 = Screw terminal - 2 pins [package=THT]
  Phase_2 = DPDT Toggle Switch
  Bypass = SPDT Toggle Switch

nets:
  N1: L1.pin_0, C1.-, C2.+
  N2: L1.pin_1, Woofer_1.pin2, R2.Pin_1, R4.Pin_1, C3.-, Input.pin2, Woofer_1_2.pin2, Phase.3, Phase.4
  N3: L2.pin_0, Input.pin1
  N4: L2.pin_1, L3.pin_1, C3.+
  N5: L3.pin_0, R3.Pin_0, Attenuation_2.6
  N6: Tweeter.pin1, Tweeter_2.pin1, Phase.5
  N7: Tweeter.pin2, Tweeter_2.pin2, Phase.2
  N8: Woofer_1.pin1, Woofer_1_2.pin1, Phase_2.3, Phase_2.4, Bypass.3
  N9: R2.Pin_0, Attenuation.1
  N10: R4.Pin_0, Attenuation_2.1
  N11: R1.Pin_0, Attenuation.6, C2.-
  N12: R1.Pin_1, Attenuation.4
  N13: R3.Pin_1, Attenuation_2.4
  N14: Attenuation.2, Attenuation.5, Phase.1, Phase.6
  N15: Attenuation_2.2, Attenuation_2.5, Bypass.2
  N16: Woofer_2.pin1, Woofer_2_2.pin1, Phase_2.5
  N17: Woofer_2.pin2, Woofer_2_2.pin2, Phase_2.2
  N18: Phase_2.1, Phase_2.6, Bypass.1

notes:
  Off
  Full
  Cut
  High Range
  Low Range

custom parts:
  DPDT Toggle Switch: DPDT Toggle Switch. On-On
  SPDT Toggle Switch: SPDT Toggle Switch. On-On
