# Fritzing sketch AAA Cap Board (saved by Fritzing 0.9.2b)
circuit board: 8.7cm x 2.1cm

parts:
  C15 = Ceramic Capacitor [capacitance=920pF voltage=50V package="0603 [SMD, multilayer]"]
  C12 = Tantalum Capacitor [capacitance=3.3µF voltage=50V package="D 7343 [SMD, tantalum]"]
  C5 = Electrolytic Capacitor [capacitance=820µF voltage=6.3V package="200 mil [THT, electrolytic]"]
  C6 = Electrolytic Capacitor [capacitance=330µF voltage=25V package="200 mil [THT, electrolytic]"]
  C3 = Electrolytic Capacitor [capacitance=10µF voltage=400V package="300 mil [THT, electrolytic]"]
  C4 = Electrolytic Capacitor [capacitance=5.6µF voltage=400V package="300 mil [THT, electrolytic]"]
  C8 = Ceramic Capacitor [capacitance=22nF voltage=16V package="200 mil [THT, multilayer]"]
  C10 = Ceramic Capacitor [capacitance=30pF voltage=50V package="100 mil [THT, multilayer]"]
  C9 = Ceramic Capacitor [capacitance=1nF voltage=50V package="200 mil [THT, multilayer]"]
  C14 = Ceramic Capacitor [capacitance=56pF voltage=50V package="100 mil [THT, multilayer]"]
  C11 = Tantalum Capacitor [capacitance=22µF voltage=50V package="100 mil [THT, tantalum]"]
  C2 = Tantalum Capacitor [capacitance=10µF voltage=16V package="A 3216 [SMD, tantalum]"]
  C13 = Tantalum Capacitor [capacitance=10µF voltage=16V package="A 3216 [SMD, tantalum]"]
  C7 = Electrolytic Capacitor [capacitance=1µF voltage=25V package="100 mil [THT, electrolytic]"]
  C1 = Ceramic Capacitor [capacitance=68pF voltage=50V package="100 mil [THT, multilayer]"]

nets:
  N1: C15.0, C12.-, C5.-, C6.-, C3.-, C4.-, C8.0, C10.0, C9.0, C14.0, C11.-, C2.-, C13.-, C7.-, C1.0
  N2: C15.1, C12.+, C5.+, C6.+, C3.+, C4.+, C8.1, C10.1, C9.1, C14.1, C11.+, C2.+, C13.+, C7.+, C1.1

notes:
  +
  -
