# Fritzing sketch Power Supply (saved by Fritzing 0.9.2b)
circuit board: 10cm x 7.5cm
breadboards: 1

parts:
  DC_Input = Power plug
  USB_Input = USB+SHIELD [package=usb-b-pth]
  Input_Fuse = Fuse with Handler [part_number=Htc-15m]
  Output_Fuse = Fuse with Handler [part_number=Htc-15m]  # not connected
  Reset = Pushbutton [package="[THT]"]  # not connected
  7805 = Voltage Regulator [package=to-220-alt]
  7812 = Voltage Regulator [package=to-220-alt]
  RS485 = male pin header, 2 pins [form="♂ (male)"]  # not connected
  XTAL1 = Crystal [frequency="16 Mhz" package=THT]  # not connected
  C1 = Ceramic Capacitor [capacitance=22pF package="100 mil [THT, multilayer]"]  # not connected
  C2 = Ceramic Capacitor [capacitance=22pF package="100 mil [THT, multilayer]"]  # not connected
  J1 = double row male pin header, 6 pins [form="♂ (male)"]  # not connected
  Blend_Micro_BLE = Blend Micro v1.0  # not connected
  MCP42100 = IC, DIP package, 14 pins [chip_label=IC]  # not connected
  MCP42100_2 = IC, DIP package, 14 pins [chip_label=IC]  # not connected
  Coarse = double row male pin header, 4 pins [form="♂ (male)"]
  Power = double row male pin header, 4 pins [form="♂ (male)"]
  Power_Relay = Relay T73
  LEDi = LED - 3mm [color="Red (633nm)" package="3 mm [THT]"]
  Ri = Resistor [tolerance=±5% resistance=1.2k package=THT]
  Pad1 = Pad [width=12 height=18 connect=center]  # not connected
  Pad2 = Pad [width=12 height=18 connect=center]  # not connected
  C3 = Electrolytic Capacitor [capacitance=10µF voltage=50V package="100 mil [THT, electrolytic]"]  # not connected
  C4 = Electrolytic Capacitor [capacitance=10µF voltage=50V package="100 mil [THT, electrolytic]"]  # not connected
  C7 = Tantalum Capacitor [capacitance=10µF voltage=50V package="100 mil [THT, tantalum]"]  # not connected
  C8 = Capacitor [part_number="50V 10uF" package=1210]  # not connected
  C9 = Capacitor [part_number="50V 10uF" package=1210]  # not connected
  LEDo = LED - 3mm [color="Red (633nm)" package="3 mm [THT]"]
  Ro = Resistor [tolerance=±5% resistance=1.2k package=THT]
  C10 = Tantalum Capacitor [capacitance=10µF voltage=50V package="100 mil [THT, tantalum]"]  # not connected
  C11 = Tantalum Capacitor [capacitance=0.1µF voltage=50V package="100 mil [THT, tantalum]"]
  C12 = Tantalum Capacitor [capacitance=0.33µF voltage=50V package="100 mil [THT, tantalum]"]
  C15 = Tantalum Capacitor [capacitance=100nF voltage=50V package="100 mil [THT, tantalum]"]  # not connected
  C16 = Tantalum Capacitor [capacitance=100nF voltage=50V package="100 mil [THT, tantalum]"]  # not connected
  C17 = Tantalum Capacitor [capacitance=0.1nF voltage=50V package="100 mil [THT, tantalum]"]
  C18 = Tantalum Capacitor [capacitance=0.33µF voltage=50V package="100 mil [THT, tantalum]"]
  USB_Power = USB Connectors [package=usb-a-h]
  Digital_Fuse = FUSE [package=fuse_5mm]
  Rotary_Encoder = Rotary Encoder [package=THT]  # not connected
  U3 = atmega328 [package=dip]  # not connected

nets:
  GND: DC_Input.GND, USB_Input.P$1, USB_Input.P$2, USB_Input.GND, Coarse.pin2, Power.pin2, LEDi.cathode, LEDo.cathode, USB_Power.GND
  N1: DC_Input.VCC, Input_Fuse.Connector1, Digital_Fuse.1
  N2: Input_Fuse.Connector2, Power_Relay.COM
  N3: 7805.GND, C11.-, C12.-
  N4: 7805.IN, 7812.IN, C12.+, C18.+, Digital_Fuse.2
  N5: 7805.OUT, C11.+
  N6: 7812.GND, C17.-, C18.-
  N7: 7812.OUT, Coarse.pin3, Power.pin3, Power_Relay.C1, C17.+
  N8: LEDi.anode, Ri.Pin_0
  N9: LEDo.anode, Ro.Pin_0

notes:
  V+
  Isense
  GND
  -
  +

custom parts:
  Blend Micro v1.0: Blend Micro is a RedBearLab Arduino at Heart integrated development board, they have "blend"ed Arduino with Bluetooth 4.0 Low Energy (aka BLE or Bluetooth Smart) into a single board. It is targeted for makers to develop low power Internet-Of-Things (IoT) projects quickly and easily. The micro-controller unit (MCU) is Atmel ATmega32u4 and the BLE chip is Nordic nRF8001. Blend Micro runs as BLE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
  Relay T73: An T73 Mini PCB Relay
