# Fritzing sketch v1 (saved by Fritzing 0.9.2b)
breadboards: 1

parts:
  L1 = Inductor [package="400 mil [THT]"]
  C2 = Electrolytic Capacitor [capacitance=22µF voltage=0.1kV package="100 mil [THT, electrolytic]"]
  L2 = Inductor [package="400 mil [THT]"]
  L3 = Inductor [package="400 mil [THT]"]
  Tweeter = Loudspeaker [part_number=8Ω]
  Woofer = Loudspeaker [part_number=8Ω]
  R2 = Resistor [tolerance=±5% resistance=20 package=THT]
  R4 = Resistor [tolerance=±5% resistance=20 package=THT]
  C3 = Electrolytic Capacitor [capacitance=10µF voltage=0.1kV package="300 mil [THT, electrolytic]"]
  C1 = Electrolytic Capacitor [capacitance=4.7µF voltage=0.1kV package="300 mil [THT, electrolytic]"]
  J1 = Screw terminal - 2 pins [package=THT]
  R1 = Resistor [tolerance=±5% resistance=2 package=THT]
  R3 = Resistor [tolerance=±5% resistance=2 package=THT]
  J2 = male pin header, 2 pins [form="♂ (male)"]
  J3 = male pin header, 2 pins [form="♂ (male)"]
  J4 = male pin header, 2 pins [form="♂ (male)"]
  J5 = male pin header, 2 pins [form="♂ (male)"]

nets:
  N1: L1.pin_0, C2.+, C1.-
  N2: L1.pin_1, Tweeter.pin2, Woofer.pin2, R2.Pin_1, R4.Pin_1, C3.-, J1.pin2
  N3: C2.-, R1.Pin_0, J2.pin1
  N4: L2.pin_0, C1.+, J1.pin1
  N5: L2.pin_1, L3.pin_1, C3.+
  N6: L3.pin_0, R3.Pin_0, J3.pin1
  N7: Tweeter.pin1, R1.Pin_1, J2.pin2, J4.pin1
  N8: Woofer.pin1, R3.Pin_1, J3.pin2, J5.pin1
  N9: R2.Pin_0, J4.pin2
  N10: R4.Pin_0, J5.pin2
