# Fritzing sketch v2 (saved by Fritzing 0.9.2b)
breadboards: 1

parts:
  L1 = Inductor [inductance=0.38mH package="400 mil [THT]"]
  L2 = Inductor [inductance=0.78mH package="400 mil [THT]"]
  L3 = Inductor [inductance=0.25mH package="400 mil [THT]"]
  Tweeter = Loudspeaker [part_number=8Ω]
  Woofer = Loudspeaker [part_number=8Ω]
  R2 = Resistor [tolerance=±5% resistance=20 package=THT]
  R4 = Resistor [tolerance=±5% resistance=20 package=THT]
  C3 = Electrolytic Capacitor [capacitance=10.61µF voltage=0.1kV package="300 mil [THT, electrolytic]"]
  C1 = Electrolytic Capacitor [capacitance=5.31µF voltage=0.1kV package="300 mil [THT, electrolytic]"]
  Input = Screw terminal - 2 pins [package=THT]
  R1 = Resistor [tolerance=±5% resistance=2 package=THT]
  R3 = Resistor [tolerance=±5% resistance=2 package=THT]
  Attenuation = DPDT Toggle Switch
  Attenuation_2 = DPDT Toggle Switch
  C2 = Electrolytic Capacitor [capacitance=15.92µF voltage=0.1kV package="300 mil [THT, electrolytic]"]
  Tweeter(s) = Screw terminal - 2 pins [package=THT]
  Woofer(s) = Screw terminal - 2 pins [package=THT]

nets:
  N1: L1.pin_0, C1.-, C2.+
  N2: L1.pin_1, Tweeter.pin2, Woofer.pin2, R2.Pin_1, R4.Pin_1, C3.-, Input.pin2, Tweeter(s).pin2, Woofer(s).pin2
  N3: L2.pin_0, C1.+, Input.pin1
  N4: L2.pin_1, L3.pin_1, C3.+
  N5: L3.pin_0, R3.Pin_0, Attenuation_2.6
  N6: Tweeter.pin1, Attenuation.2, Attenuation.5, Tweeter(s).pin1
  N7: Woofer.pin1, Attenuation_2.2, Attenuation_2.5, Woofer(s).pin1
  N8: R2.Pin_0, Attenuation.1
  N9: R4.Pin_0, Attenuation_2.1
  N10: R1.Pin_0, Attenuation.6, C2.-
  N11: R1.Pin_1, Attenuation.4
  N12: R3.Pin_1, Attenuation_2.4

notes:
  Off
  Full
  Cut
  High Range
  Low Range

custom parts:
  DPDT Toggle Switch: DPDT Toggle Switch. On-On
